// Logisim project parallel.circ as structural Verilog: 2 circuits, main circuit data_path
module data_path (
  input  in_1,
  input  shift,
  input  in_3,
  input  in_4,
  input  in_5,
  input  clk,
  input  reset,
  input  in_8,
  input  in_9,
  input  in_10,
  input  [7:0] in_11,
  input  [7:0] \const ,
  input  load_const,
  output mult_ready,
  output [15:0] Result,
  output RR
);

  wire and_1_out, and_2_out, or_1_out, or_2_out, shift_register_1_p4, shift_register_1_p14,
       shift_register_1_p15, shift_register_1_p16, shift_register_1_p17, shift_register_1_p18,
       shift_register_1_p19, shift_register_1_p20, shift_register_2_p9, shift_register_2_p10,
       shift_register_2_p11;
  wire [7:0] multiplexer_1_out, shift_register_3_p4, xor_8_out;
  wire [15:0] adder_1_out, multiplexer_2_out, undriven;

  Multiplexer #(.width(8)) multiplexer_1 (.in0(in_11), .in1(\const ), .out(multiplexer_1_out), .sel(load_const));
  // Shift_Register shift_register_1: pin names not known; wires that end beside it: in_3, shift, clk, shift_register_1_p4, multiplexer_1_out[7], multiplexer_1_out[6], multiplexer_1_out[5], multiplexer_1_out[4], multiplexer_1_out[3], multiplexer_1_out[2], multiplexer_1_out[1], multiplexer_1_out[0], shift_register_1_p4, shift_register_1_p14, shift_register_1_p15, shift_register_1_p16, shift_register_1_p17, shift_register_1_p18, shift_register_1_p19, shift_register_1_p20
  // Shift_Register #(.length(3)) shift_register_2: pin names not known; wires that end beside it: in_9, in_8, clk, 1'b0, 1'b0, multiplexer_1_out[2], multiplexer_1_out[1], multiplexer_1_out[0], shift_register_2_p9, shift_register_2_p10, shift_register_2_p11
  nor nor_1 (mult_ready, shift_register_1_p4, shift_register_1_p14, shift_register_1_p15, shift_register_1_p16, shift_register_1_p17, shift_register_1_p18, shift_register_1_p19, shift_register_1_p20);
  or or_1 (or_1_out, shift_register_2_p9, shift_register_2_p10, shift_register_2_p11);
  and and_1 (and_1_out, shift_register_1_p20, shift);
  and and_2 (and_2_out, or_1_out, in_8);
  not not_1 (RR, or_1_out);
  // Shift_Register #(.length(16)) shift_register_3: pin names not known; wires that end beside it: in_5, clk, 1'b0, shift_register_3_p4, multiplexer_1_out, shift
  xor xor_1 (xor_8_out[7], in_1, shift_register_3_p4[7]);
  or or_2 (or_2_out, and_1_out, in_10);
  xor xor_2 (xor_8_out[6], in_1, shift_register_3_p4[6]);
  xor xor_3 (xor_8_out[5], in_1, shift_register_3_p4[5]);
  // Shift_Register #(.length(16)) shift_register_4: pin names not known; wires that end beside it: multiplexer_1_out[7], or_2_out, and_2_out, clk, adder_1_out[15], reset
  xor xor_4 (xor_8_out[4], in_1, shift_register_3_p4[4]);
  xor xor_5 (xor_8_out[3], in_1, shift_register_3_p4[3]);
  xor xor_6 (xor_8_out[2], in_1, shift_register_3_p4[2]);
  Adder #(.width(16)) adder_1 (.a(multiplexer_2_out), .b(Result), .out(adder_1_out), .cin(in_4));  // open: cout
  xor xor_7 (xor_8_out[1], in_1, shift_register_3_p4[1]);
  xor xor_8 (xor_8_out[0], in_1, shift_register_3_p4[0]);
  Multiplexer #(.width(16)) multiplexer_2 (
    .in0(undriven), .in1({{9{xor_8_out[7]}}, xor_8_out[6:0]}), .out(multiplexer_2_out), .sel(in_10));

  // Other names for the same wires on the sheet: add = in_10; invert = in_1; load_A = in_5; load_B = in_3;
  //   load_C = in_9; multiply = shift; plus_one = in_4; shift_C = in_8
endmodule

module number_loader (
  input  clk,
  input  reset,
  input  [7:0] number,
  input  load_enable,
  input  [1:0] register_selector,
  output [7:0] x,
  output [7:0] y,
  output [7:0] z,
  output [7:0] t
);

  wire demultiplexer_1_out0, demultiplexer_1_out1, demultiplexer_1_out2, demultiplexer_1_out3;

  Demultiplexer #(.select(2)) demultiplexer_1 (
    .out0(demultiplexer_1_out0), .out1(demultiplexer_1_out1), .out2(demultiplexer_1_out2),
    .out3(demultiplexer_1_out3), .in(load_enable), .sel(register_selector));
  Register register_1 (.D(number), .en(demultiplexer_1_out0), .clk(clk), .Q(x), .clr(reset));
  Register register_2 (.D(number), .en(demultiplexer_1_out1), .clk(clk), .Q(y), .clr(reset));
  Register register_3 (.D(number), .en(demultiplexer_1_out2), .clk(clk), .Q(z), .clr(reset));
  Register register_4 (.D(number), .en(demultiplexer_1_out3), .clk(clk), .Q(t), .clr(reset));
endmodule
